# Fritzing sketch TFTDisplayButtonLed (saved by Fritzing 0.9.4)
breadboards: 1

parts:
  U1 = ESP32S-HiLetgo [part_number=ESP32S-HiLetgo]
  TFT1 = Color 320x240 TFT Display, ILI9341 Controller Chip
  S1 = Momentary Switch [package=ksa_sealed_tac_switch]
  S2 = Momentary Switch [package=ksa_sealed_tac_switch]
  S3 = Momentary Switch [package=ksa_sealed_tac_switch]
  LED1 = LED - 3mm [color="White (4500K)" package="3 mm [THT]"]
  LED2 = LED - 3mm [color="Blue (430nm)" package="3 mm [THT]"]
  LED3 = LED - 3mm [color="Red (633nm)" package="3 mm [THT]"]
  R1 = Resistor [tolerance=±5% resistance=220 package=THT]
  R2 = Resistor [tolerance=±5% resistance=220 package=THT]
  R3 = Resistor [tolerance=±5% resistance=220 package=THT]
  R4 = Resistor [tolerance=±5% resistance=330 package=THT]
  R5 = Resistor [tolerance=±5% resistance=330 package=THT]
  R6 = Resistor [tolerance=±5% resistance=330 package=THT]

nets:
  N1: U1.3.3, TFT1.VCC, S1.1, S2.1, S3.1
  N2: U1.GPIO25, R3.Pin_0
  N3: U1.GPIO26, R2.Pin_0
  N4: U1.GPIO27, R1.Pin_0
  N5: U1.GPIO14, TFT1.Reset
  GND: U1.GND, TFT1.GND, LED1.cathode, LED2.cathode, LED3.cathode, R4.Pin_1, R6.Pin_1
  N6: U1.VIN, TFT1.LED
  N7: U1.GPIO15, TFT1.D/C
  N8: U1.GPIO4, S2.3, R5.Pin_0
  N9: U1.GPIO16, S3.3, R6.Pin_0
  N10: U1.GPIO17, TFT1.CS
  N11: U1.GPIO5, S1.3, R4.Pin_0
  N12: U1.GPIO18, TFT1.SCK
  N13: U1.GPIO19, TFT1.SDO_(MISO)
  N14: U1.GPIO23, TFT1.SDI_(MOSI)
  N15: LED1.anode, R3.Pin_1
  N16: LED2.anode, R2.Pin_1
  N17: LED3.anode, R1.Pin_1

custom parts:
  ESP32S-HiLetgo: HiLetgo ESP-WROOM-32 ESP32 ESP-32S Development Board 2.4GHz Dual-Mode WiFi + Bluetooth Dual Cores Microcontroller The ESP32 integrated with Antenna switches, RF Balun, power amplifiers, low-noise amplifiers, filters, and management modules, and the entire solution occupies the least area of PCB. 2.4 GHz Wi-Fi plus Bluetooth dual-mode chip, with TSMC Ultra-low power consumption 40nm technology,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
  Color 320x240 TFT Display, ILI9341 Controller Chip: 2.2" TFT Display with ILI9341 Controller
